# Fritzing sketch circuit diagram (saved by Fritzing 0.9.4)

parts:
  S1 = Pololu QTR-8 Reflectabce Sensor array [package=THT]
  Part1 = Arduino Uno (Rev3)
  M1 = L293D Motor Driver
  M2 = DC Motor
  M3 = DC Motor
  M4 = DC Motor
  M5 = DC Motor
  BAT1 = BC9VPC [package=bc9vpc]

nets:
  N1: S1.pin1, Part1.GND, BAT1.V-
  N2: S1.pin2, S1.pin14, Part1.5V
  N3: S1.pin5, Part1.D8
  N4: S1.pin6, Part1.D7
  N5: S1.pin7, Part1.D6_PWM
  N6: S1.pin8, Part1.D5_PWM
  N7: S1.pin9, Part1.D4
  N8: S1.pin10, Part1.D3_PWM
  N9: S1.pin11, Part1.D2
  N10: S1.pin12, Part1.D1/TX
  N11: Part1.D9_PWM, M1.connector5
  N12: Part1.D10_PWM/SS, M1.connector6
  N13: Part1.D11_PWM/MOSI, M1.connector7
  N14: Part1.D12/MISO, M1.connector8
  N15: Part1.VIN, BAT1.V+
  N16: M1.connector9, M2.pin_1, M3.pin_1
  N17: M1.connector10, M2.pin_2, M3.pin_2
  N18: M1.connector11, M4.pin_1, M5.pin_1
  N19: M1.connector12, M4.pin_2, M5.pin_2
